# Fritzing sketch BOARD1 (saved by Fritzing 1.0.4)
breadboards: 2

parts:
  Part1 = Arduino MKR WAN 1310
  Module1 = Relay
  Part2 = Soil Moisture Sensor
  DHT1 = DHT22 Humidity and Temperature Sensor
  ds18b20_probe1 = ds18b20 probe
  Module2 = Relay
  Water_Level_Sensor1 = Water Level Sensor
  LED4 = smd LED [color="Green (565nm)" package="0805 [SMD]"]
  LED5 = smd LED [color="Red (633nm)" package="0805 [SMD]"]
  LED6 = smd LED [color="Yellow (592nm)" package="0805 [SMD]"]
  Mod1 = Passive Buzzer
  Mod2 = L298N DC motor driver
  TEC1 = TEC1-12706 Thermo Electric Cooler [package=THT]
  Part5 = Arduino MKR WAN 1310
  TEC2 = TEC1-12706 Thermo Electric Cooler [package=THT]
  Water_Level_Sensor2 = Water Level Sensor
  LED7 = smd LED [color="Yellow (592nm)" package="0805 [SMD]"]
  LED8 = smd LED [color="Red (633nm)" package="0805 [SMD]"]
  LED9 = smd LED [color="Green (565nm)" package="0805 [SMD]"]
  Mod3 = Passive Buzzer
  Mod4 = L298N DC motor driver
  Part6 = Arduino MKR WAN 1310
  Module3 = Relay
  Module4 = Relay
  Part7 = Soil Moisture Sensor
  DHT2 = DHT22 Humidity and Temperature Sensor
  ds18b20_probe2 = ds18b20 probe
  S1 = PH meter [package=THT]
  esp1 = ESP32 DevKitc V4

nets:
  N1: Part1.D0, Mod2.IN1
  N2: Part1.D1, Mod2.IN2
  GND: Part1.GND, Module1.ground, Part2.GND, DHT1.GND, ds18b20_probe1.pin3, Module2.ground, Water_Level_Sensor1.GND, LED4.cathode, Mod1.-, S1.pin3
  N3: Part1.D2, DHT1.DATA
  N4: Part1.D3~, Module1.signal
  N5: Part1.D4, Mod1.S
  N6: Part1.D5~, Module2.signal
  N7: Part1.D6~, LED4.anode
  N8: Part1.D7, LED6.anode
  N9: Part1.D8, LED5.anode
  N10: Part1.D9~, ds18b20_probe1.pin2
  N11: Part1.D10~, Mod2.ENA
  VCC: Part1.D11/MOSI, Part1.+5V, Module1.power, Part2.VCC, DHT1.VDD, ds18b20_probe1.pin1, Module2.power, Water_Level_Sensor1.VCC, Mod1.NC, S1.pin2
  N12: Part1.A2, Water_Level_Sensor1.SIG
  N13: Part1.A1, S1.pin1
  N14: Part1.A0, Part2.SIG
  N15: Mod2.OUT1, TEC1.+
  N16: Mod2.OUT2, TEC1.-
  N17: Part5.RESET, Part5.D14/TX, esp1.IO16, esp1.IO17
  N18: TEC2.-, Mod4.OUT2
  N19: TEC2.+, Mod4.OUT1
  N20: Water_Level_Sensor2.SIG, Part6.A2
  VCC_2: Water_Level_Sensor2.VCC, Mod3.NC, Part6.D11/MOSI, Part6.+5V, Module4.power, Part7.VCC, DHT2.VDD, ds18b20_probe2.pin1
  GND_2: Water_Level_Sensor2.GND, LED9.cathode, Mod3.-, Part6.GND, Module3.ground, Module4.ground, Part7.GND, DHT2.GND, ds18b20_probe2.pin3
  N21: LED7.anode, Part6.D7
  N22: LED8.anode, Part6.D8
  N23: LED9.anode, Part6.D6~
  N24: Mod3.S, Part6.D4
  N25: Mod4.ENA, Part6.D10~
  N26: Mod4.IN1, Part6.D0
  N27: Mod4.IN2, Part6.D1
  N28: Part6.D2, DHT2.DATA
  N29: Part6.D3~, Module4.signal
  N30: Part6.D5~, Module3.signal
  N31: Part6.D9~, ds18b20_probe2.pin2
  N32: Part6.A0, Part7.SIG

notes:
  CIRCUIT ONE
  CIRCUIT TWO
  CIRCUIT THREE

custom parts:
  Arduino MKR WAN 1310: The Arduino MKR WAN 1310 board provides a practical and cost effective solution to add LoRa® connectivity to projects requiring low power. This open source board can be connected to: the Arduino IoT Cloud, your own LoRa® network using the Arduino LoRa® PRO Gateway, existing LoRaWAN™ infrastructure like The Things Network, or even other boards using the direct connectivity mode.
  Water Level Sensor: A water level sensor. This sensor operates at 3V to 5V. The Sig (signal) pin outputs an analogue signal that is in proportion to the amount of water in contact with the sensor.
  L298N DC motor driver: 2x DC motor driver with 78M05 positive voltage regulator (7..35 V) L298N: max 46 V, 2 A Set 5 V Enable jumper to enable 5 V regultor (needed for the L298N) and +5 V output at screw terminal or supply external +5 V at screw terminal Set ENA and/or ENB to +5 V to enable motor permanently or supply ENA and/or ENB with PWM signal IN1 and IN2 set rotation directory for motor A (OUT1/OUT2) IN2 and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
  ESP32 DevKitc V4: ESP32-DevKitC board with ESP32-WROOM-32 module. ESP32-DevKitC V4 is a small-sized ESP32-based development board produced by Espressif. Most of the pins on the ESP module are broken out to the pin headers on the board. The pins D0, D1, D2, D3, CMD and CLK are used internally for communication between ESP32 and SPI flash memory. They are grouped on both sides near the USB connector. Avoid using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
